# Fritzing sketch teplitsa_scheme (saved by Fritzing 0.9.5d)
breadboards: 1

parts:
  U1 = ESP32S-HiLetgo [part_number=ESP32S-HiLetgo]
  U2 = RELAY [package=relay-jzc]
  U3 = RELAY [package=relay-jzc]
  JACK1 = 2.1mm Barrel Jack with Terminal Block
  Компонент1 = Soil Moisture Sensor  # not connected
  R1 = Resistor [tolerance=±5% resistance=220 package="0805 [SMD]"]  # not connected
  WATER_PUMP1 = water pump/motor  # not connected
  M1 = RioRand LM2596
  M2 = RioRand LM2596

nets:
  N1: U1.GPIO35, U1.GPIO32, U2.MAIN
  N2: U1.GPIO33, U3.MAIN
  N3: U1.GND, U2.COIL1, U3.COIL1, JACK1.NEG, M1.Pin_2, M1.Pin_4, M2.Pin_2, M2.Pin_4
  N4: U2.COIL2, M2.Pin_3
  N5: U3.COIL2, M1.Pin_3
  N6: JACK1.POS, M1.Pin_1, M2.Pin_1

custom parts:
  ESP32S-HiLetgo: HiLetgo ESP-WROOM-32 ESP32 ESP-32S Development Board 2.4GHz Dual-Mode WiFi + Bluetooth Dual Cores Microcontroller The ESP32 integrated with Antenna switches, RF Balun, power amplifiers, low-noise amplifiers, filters, and management modules, and the entire solution occupies the least area of PCB. 2.4 GHz Wi-Fi plus Bluetooth dual-mode chip, with TSMC Ultra-low power consumption 40nm technology,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
  water pump/motor: WATER PUMP BY ARDUBLOCKTR
